# Fritzing sketch PhotoLeds (saved by Fritzing 0.6.4b)
breadboards: 1

parts:
  Arduino1 = Arduino
  R1 = Photocell (LDR) [package=THT]
  R2 = Resistor [tolerance=±5% resistance=10k package=THT]
  LED1 = LED - 5mm [color="Red (633nm)" package="5 mm [THT]"]
  LED2 = LED - 5mm [color="Red (633nm)" package="5 mm [THT]"]
  LED3 = LED - 5mm [color="Red (633nm)" package="5 mm [THT]"]
  R3 = Resistor [tolerance=±5% resistance=10k package=THT]
  R4 = Resistor [tolerance=±5% resistance=10k package=THT]
  R5 = Resistor [tolerance=±5% resistance=10k package=THT]

nets:
  N1: Arduino1.GND, R2.Pin_1, LED1.cathode, LED2.cathode, LED3.cathode
  N2: Arduino1.D6, R3.Pin_0
  N3: Arduino1.D5, R4.Pin_0
  N4: Arduino1.D3, R5.Pin_0
  N5: Arduino1.+5V, R1.pin_1
  N6: Arduino1.A0, R1.pin_0, R2.Pin_0
  N7: LED1.anode, R5.Pin_1
  N8: LED2.anode, R4.Pin_1
  N9: LED3.anode, R3.Pin_1
