# Fritzing sketch PiLCD (saved by Fritzing 0.9.2b)
breadboards: 1

parts:
  R1 = TRIMPOT [package=3362u-2]
  Part1 = Arduino Uno (Rev3)
  LCD1 = LCD screen

nets:
  GND: R1.CCW, Part1.GND, LCD1.VSS, LCD1.R/W, LCD1.LED-
  N1: R1.WIPER, LCD1.V0
  3V3: R1.CW, Part1.3V3, LCD1.VDD, LCD1.LED+
  N2: Part1.D11_PWM/MOSI, LCD1.E
  N3: Part1.D12/MISO, LCD1.RS
  N4: Part1.D2, LCD1.DB7
  N5: Part1.D3_PWM, LCD1.DB6
  N6: Part1.D4, LCD1.DB5
  N7: Part1.D5_PWM, LCD1.DB4
