# Fritzing sketch PiSeg (saved by Fritzing 0.7.0b)
breadboards: 1

parts:
  Arduino1 = Arduino
  7_Segment1 = 7 Segment Display [part_number=276-0075]
  R1 = Resistor [tolerance=±5% resistance=100 package=THT]
  R4 = Resistor [tolerance=±5% resistance=100 package=THT]
  R5 = Resistor [tolerance=±5% resistance=100 package=THT]
  R6 = Resistor [tolerance=±5% resistance=100 package=THT]
  R7 = Resistor [tolerance=±5% resistance=100 package=THT]
  R8 = Resistor [tolerance=±5% resistance=100 package=THT]
  R9 = Resistor [tolerance=±5% resistance=100 package=THT]
  R10 = Resistor [tolerance=±5% resistance=100 package=THT]

nets:
  N1: Arduino1.GND, 7_Segment1.common_cathode
  N2: Arduino1.D9, R4.Pin_0
  N3: Arduino1.D8, R5.Pin_0
  N4: Arduino1.D7, R6.Pin_0
  N5: Arduino1.D6, R7.Pin_0
  N6: Arduino1.D5, R8.Pin_0
  N7: Arduino1.D4, R9.Pin_0
  N8: Arduino1.D3, R10.Pin_0
  N9: Arduino1.D2, R1.Pin_0
  N10: 7_Segment1.Segment_A#1, R1.Pin_1
  N11: 7_Segment1.Segment_F, R10.Pin_1
  N12: 7_Segment1.Segment_E, R9.Pin_1
  N13: 7_Segment1.Segment_D, R8.Pin_1
  N14: 7_Segment1.Segment_DP, R7.Pin_1
  N15: 7_Segment1.Segment_C, R4.Pin_1
  N16: 7_Segment1.Segment_B, R6.Pin_1
  N17: 7_Segment1.Segment_A#10, R5.Pin_1
