# Fritzing sketch Replay (saved by Fritzing 0.6.4b)
breadboards: 1

parts:
  Arduino1 = Arduino
  R1 = Resistor [tolerance=±5% resistance=1k package=THT]
  R2 = Resistor [tolerance=±5% resistance=100 package=THT]
  R3 = Resistor [tolerance=±5% resistance=10k package=THT]
  S1 = Pushbutton [package="[THT]"]
  LED1 = LED - 5mm [color="Red (633nm)" package="5 mm [THT]"]

nets:
  N1: Arduino1.D13, R1.Pin_0
  N2: Arduino1.D8, R2.Pin_1
  N3: Arduino1.+5V, R2.Pin_0, R3.Pin_0, S1.Pin_1, S1.Pin_2, S1.Pin_3, S1.Pin_4
  N4: Arduino1.GND, R3.Pin_1, LED1.cathode
  N5: R1.Pin_1, LED1.anode
